# Fritzing sketch course 8 (saved by Fritzing 1.0.5)
breadboards: 1

parts:
  Part1 = Arduino Uno (Rev3)
  SEN1 = US-100 Ultrasonic Distance Sensor
  LED1 = LED - 3mm [color="Red (633nm)" current=0.030A package="3 mm [THT]"]
  R1 = Resistor [tolerance=±5% power=0.25W resistance=220 package=THT]

nets:
  N1: Part1.D11_PWM/MOSI, SEN1.TRIG
  N2: Part1.D12/MISO, SEN1.ECHO
  N3: Part1.D5_PWM, R1.Pin_1
  5V: Part1.5V, SEN1.VCC
  GND: Part1.GND, SEN1.GND, SEN1.GND-2, LED1.cathode
  N4: LED1.anode, R1.Pin_0
